// Logisim project CONTROL_UNITS.circ as structural Verilog
module PC (
  input  C,
  input  Z,
  input  T0,
  input  T1,
  input  T3,
  input  T4,
  input  M196,
  input  M197,
  input  M198,
  input  M199,
  input  M200,
  input  M201,
  input  M202,
  input  M203,
  input  M204,
  input  M205,
  input  M206,
  input  M207,
  input  M208,
  input  M209,
  input  M210,
  input  M211,
  input  M212,
  input  M213,
  output PC_BUS,
  output PC_INC,
  output PC_LOAD
);

  wire and_1_out, and_2_out, and_3_out, and_4_out, and_5_out, and_6_out, and_7_out, and_8_out, and_9_out,
       and_10_out, and_11_out, and_12_out, and_13_out, and_14_out, and_15_out, and_16_out, and_17_out,
       or_1_out, or_2_out;

  and and_1 (and_1_out, M199, Z);
  and and_2 (and_2_out, M202, ~Z);  // AND_Gate
  and and_3 (and_3_out, M205, C, ~Z);  // AND_Gate
  and and_4 (and_4_out, M208, ~C, Z);  // AND_Gate
  and and_5 (and_5_out, M211, Z, C);
  and and_6 (and_6_out, M200, Z);
  and and_7 (and_7_out, M201, Z);
  and and_8 (and_8_out, M203, ~Z);  // AND_Gate
  and and_9 (and_9_out, M204, ~Z);  // AND_Gate
  and and_10 (and_10_out, M206, C, ~Z);  // AND_Gate
  and and_11 (and_11_out, M207, C, ~Z);  // AND_Gate
  and and_12 (and_12_out, M209, ~C, Z);  // AND_Gate
  and and_13 (and_13_out, M210, ~C, Z);  // AND_Gate
  and and_14 (and_14_out, M212, C, Z);
  and and_15 (and_15_out, M213, C, Z);
  or or_1 (or_1_out, M196, and_1_out, and_2_out, and_3_out, and_4_out, and_5_out);
  and and_16 (and_16_out, or_1_out, T4);
  or or_2 (or_2_out, M197, M198, and_6_out, and_7_out, and_8_out, and_9_out, and_10_out, and_11_out, and_12_out, and_13_out, and_14_out, and_15_out);
  and and_17 (and_17_out, or_2_out, T3);
  or or_3 (PC_LOAD, and_16_out, and_17_out);

  assign PC_BUS = T0;
  assign PC_INC = T1;
endmodule

module IR (
  input  T1,
  input  T2,
  input  T3,
  input  M190,
  input  M191,
  input  M192,
  input  M193,
  input  M194,
  output IR_BUS,
  output IR_LOAD
);

  wire and_1_out, or_1_out;

  or or_1 (or_1_out, M194, M193, M192, M191, M190);
  and and_1 (and_1_out, or_1_out, T3);
  or or_2 (IR_BUS, and_1_out, T2);

  assign IR_LOAD = T1;
endmodule

module AR (
  input  C,
  input  Z,
  input  T0,
  input  T2,
  input  T3,
  input  T4,
  input  M0,
  input  M1,
  input  M2,
  input  M3,
  input  M4,
  input  M17,
  input  M18,
  input  M19,
  input  M20,
  input  M21,
  input  M34,
  input  M35,
  input  M36,
  input  M37,
  input  M38,
  input  M51,
  input  M52,
  input  M53,
  input  M54,
  input  M55,
  input  M68,
  input  M69,
  input  M70,
  input  M71,
  input  M72,
  input  M85,
  input  M86,
  input  M87,
  input  M88,
  input  M89,
  input  M102,
  input  M103,
  input  M104,
  input  M105,
  input  M106,
  input  M119,
  input  M120,
  input  M121,
  input  M122,
  input  M123,
  input  M136,
  input  M137,
  input  M138,
  input  M139,
  input  M140,
  input  M153,
  input  M154,
  input  M155,
  input  M156,
  input  M157,
  input  M170,
  input  M171,
  input  M172,
  input  M173,
  input  M174,
  input  M180,
  input  M181,
  input  M182,
  input  M183,
  input  M184,
  input  M196,
  input  M197,
  input  M199,
  input  M200,
  input  M202,
  input  M203,
  input  M205,
  input  M206,
  input  M208,
  input  M209,
  input  M211,
  input  M212,
  output AR_LOAD,
  output AR_BUS
);

  wire and_1_out, and_2_out, and_3_out, and_4_out, and_5_out, and_6_out, and_7_out, and_8_out, and_9_out,
       and_10_out, and_11_out, and_12_out, and_13_out, or_1_out, or_2_out, or_3_out, or_4_out;

  and and_1 (and_1_out, M196, T4);
  and and_2 (and_2_out, M197, T3);
  and and_3 (and_3_out, M199, T4, Z);
  and and_4 (and_4_out, M200, T3, Z);
  and and_5 (and_5_out, M202, T4, ~Z);  // AND_Gate
  and and_6 (and_6_out, M203, T3, ~Z);  // AND_Gate
  and and_7 (and_7_out, M205, T4, ~Z, C);  // AND_Gate
  and and_8 (and_8_out, M206, T3, ~Z, C);  // AND_Gate
  and and_9 (and_9_out, M208, T4, Z, ~C);  // AND_Gate
  and and_10 (and_10_out, M209, T3, Z, ~C);  // AND_Gate
  and and_11 (and_11_out, M211, T4, Z, C);
  and and_12 (and_12_out, M212, T3, Z, C);
  or or_1 (or_1_out, M211, M208, M205, M202, M199, M196, M184, M183, M182, M181, M180, M174, M173, M172, M171, M170, M157, M156, M155, M154, M153, M140);
  or or_2 (or_2_out, M139, M138, M137, M136, M123, M122, M121, M120, M119, M106, M105, M104, M103, M102, M89, M88, M87, M86, M85, M72, M71, M70);
  or or_3 (or_3_out, M69, M68, M55, M54, M53, M52, M51, M38, M37, M36, M35, M34, M21, M20, M19, M18, M17, M4, M3, M2, M1, M0);
  or or_4 (or_4_out, or_1_out, or_2_out, or_3_out);
  or or_5 (AR_BUS, and_1_out, and_2_out, and_3_out, and_4_out, and_5_out, and_6_out, and_7_out, and_8_out, and_9_out, and_10_out, and_11_out, and_12_out);
  and and_13 (and_13_out, or_4_out, T3);
  or or_6 (AR_LOAD, and_13_out, T2, T0);
endmodule

module DR (
  input  T3,
  input  T4,
  input  T5,
  input  M0,
  input  M1,
  input  M2,
  input  M3,
  input  M4,
  input  M5,
  input  M6,
  input  M7,
  input  M8,
  input  M9,
  input  M15,
  input  M17,
  input  M18,
  input  M19,
  input  M20,
  input  M21,
  input  M22,
  input  M23,
  input  M24,
  input  M25,
  input  M26,
  input  M32,
  input  M34,
  input  M35,
  input  M36,
  input  M37,
  input  M38,
  input  M39,
  input  M40,
  input  M41,
  input  M42,
  input  M43,
  input  M49,
  input  M51,
  input  M52,
  input  M53,
  input  M54,
  input  M55,
  input  M56,
  input  M57,
  input  M58,
  input  M59,
  input  M60,
  input  M66,
  input  M68,
  input  M69,
  input  M70,
  input  M71,
  input  M72,
  input  M73,
  input  M74,
  input  M75,
  input  M76,
  input  M77,
  input  M83,
  input  M85,
  input  M86,
  input  M87,
  input  M88,
  input  M89,
  input  M90,
  input  M91,
  input  M92,
  input  M93,
  input  M94,
  input  M100,
  input  M102,
  input  M103,
  input  M104,
  input  M105,
  input  M106,
  input  M107,
  input  M108,
  input  M109,
  input  M110,
  input  M111,
  input  M117,
  input  M119,
  input  M120,
  input  M121,
  input  M122,
  input  M123,
  input  M124,
  input  M125,
  input  M126,
  input  M127,
  input  M128,
  input  M134,
  input  M136,
  input  M137,
  input  M138,
  input  M139,
  input  M140,
  input  M141,
  input  M142,
  input  M143,
  input  M144,
  input  M145,
  input  M151,
  input  M153,
  input  M154,
  input  M155,
  input  M156,
  input  M157,
  input  M158,
  input  M159,
  input  M160,
  input  M161,
  input  M162,
  input  M168,
  input  M170,
  input  M171,
  input  M172,
  input  M173,
  input  M174,
  input  M175,
  input  M176,
  input  M177,
  input  M178,
  input  M179,
  output DR_LOAD,
  output DR_BUS
);

  wire and_1_out, and_2_out, and_3_out, and_4_out, or_1_out, or_2_out, or_3_out, or_4_out, or_5_out,
       or_6_out, or_7_out, or_8_out, or_9_out;

  or or_1 (or_1_out, M179, M178, M177, M176, M175);
  or or_2 (or_2_out, M174, M173, M172, M171, M170);
  or or_3 (or_3_out, M179, M178, M177, M176, M175, M168, M162, M161, M160, M159, M158, M151, M145, M144, M143, M142, M141, M134, M128, M127, M126, M125);
  or or_4 (or_4_out, M124, M117, M111, M110, M109, M108, M107, M100, M94, M93, M92, M91, M90, M83, M77, M76, M75, M74, M73, M66, M60, M59);
  or or_5 (or_5_out, M58, M57, M56, M49, M43, M42, M41, M40, M39, M32, M26, M25, M24, M23, M22, M15, M9, M8, M7, M6, M5);
  or or_6 (or_6_out, M174, M173, M172, M171, M170, M157, M156, M155, M154, M153, M140, M139, M138, M137, M136, M123, M122, M121, M120, M119, M106, M105, M104, M103, M102, M89, M88, M87);
  or or_7 (or_7_out, M86, M85, M72, M71, M70, M69, M68, M55, M54, M53, M52, M51, M38, M37, M36, M35, M34, M21, M20, M19, M18, M17, M4, M3, M2, M1, M0);
  and and_1 (and_1_out, or_1_out, T4);
  and and_2 (and_2_out, T5, or_2_out);
  or or_8 (or_8_out, or_3_out, or_4_out, or_5_out);
  and and_3 (and_3_out, or_8_out, T3);
  or or_9 (or_9_out, or_6_out, or_7_out);
  and and_4 (and_4_out, or_9_out, T4);
  or or_10 (DR_BUS, and_1_out, and_2_out);
  or or_11 (DR_LOAD, and_3_out, and_4_out);
endmodule
