// Logisim project Microprocessor.circ as structural Verilog: 1 circuit, main circuit CPU
module CPU (
);

  wire alu_1_cout, alu_1_zero, and_1_out, clock_1_out, control_unit_1_p1, control_unit_1_p2,
       control_unit_1_p26, control_unit_1_p27, undriven, undriven_2, undriven_3, undriven_4, undriven_5,
       undriven_6, undriven_7, undriven_8, undriven_9, undriven_15, undriven_16, undriven_17, undriven_18,
       undriven_19, undriven_20, undriven_21, undriven_22, undriven_23, undriven_24, undriven_25;
  wire [2:0] control_unit_1_p28;
  wire [4:0] control_unit_1_p3;
  wire [6:0] control_unit_1_p19;
  wire [7:0] instruction_register_1_output_2;
  wire [8:0] undriven_10, undriven_11, undriven_12, undriven_13, undriven_14;
  wire [10:0] control_unit_1_p18;
  wire [15:0] alu_1_ax_4, alu_1_bx_4, alu_1_cx_4, alu_1_dx_4, alu_1_ex_4, general_purpose_1_output,
       general_purpose_2_output, general_purpose_3_output, general_purpose_4_output,
       general_purpose_5_output, instruction_register_1_output, multiplexer_1_out, special_purpose_1_output,
       special_purpose_2_output, special_purpose_3_output;
  wire [23:0] controlled_buffer_1_out, ram_1_data;

  Clock clock_1 (.out(clock_1_out));
  // CONTROL_UNIT control_unit_1: pin names not known; wires that end beside it: control_unit_1_p1, control_unit_1_p2, control_unit_1_p3[0], control_unit_1_p3[1], control_unit_1_p3[2], control_unit_1_p3[3], control_unit_1_p3[4], control_unit_1_p18[10], control_unit_1_p18[9], control_unit_1_p18[8], control_unit_1_p18[7], control_unit_1_p18[6], control_unit_1_p18[5], control_unit_1_p18[4], control_unit_1_p18[3], control_unit_1_p18[2], control_unit_1_p18[1], control_unit_1_p18[0], control_unit_1_p19[0], control_unit_1_p19[1], control_unit_1_p19[2], control_unit_1_p19[3], control_unit_1_p19[4], control_unit_1_p19[5], control_unit_1_p19[6], control_unit_1_p26, control_unit_1_p27, control_unit_1_p28, undriven_10[8], undriven_10[6], undriven_10[5], undriven_10[4], undriven_10[3], undriven_10[2], undriven_10[1]
  and and_1 (and_1_out, ~undriven, clock_1_out);  // AND_Gate
  FLAG flag_1 (
    .INPUT(alu_1_zero), .CLK(and_1_out), .LOAD(undriven_15), .CLR(undriven_7), .CML(undriven_8),
    .OUTPUT(control_unit_1_p2));
  FLAG flag_2 (
    .INPUT(alu_1_cout), .CLK(and_1_out), .LOAD(undriven_16), .CLR(undriven_9), .CML(undriven_17),
    .OUTPUT(control_unit_1_p1));
  ALU alu_1 (
    .Cin(control_unit_1_p1), .AX_2(control_unit_1_p3[0]), .BX_2(control_unit_1_p3[1]),
    .CX_2(control_unit_1_p3[2]), .DX_2(control_unit_1_p3[3]), .EX_2(control_unit_1_p3[4]), .DR_2(1'b0),
    .IR_2(1'b0), .AX_3(control_unit_1_p19[0]), .BX_3(control_unit_1_p19[1]), .CX_3(control_unit_1_p19[2]),
    .DX_3(control_unit_1_p19[3]), .EX_3(control_unit_1_p19[4]), .DR_3(control_unit_1_p19[5]),
    .IR_3(control_unit_1_p19[6]), .AX(general_purpose_1_output), .BX(general_purpose_2_output),
    .CX(general_purpose_3_output), .DX(general_purpose_4_output), .EX(general_purpose_5_output),
    .DR(special_purpose_3_output), .IR(instruction_register_1_output), .AND(control_unit_1_p18[10]),
    .OR(control_unit_1_p18[9]), .XOR(control_unit_1_p18[8]), .ADD(control_unit_1_p18[7]),
    .ADC(control_unit_1_p18[6]), .SUB(control_unit_1_p18[5]), .SBB(control_unit_1_p18[4]),
    .MUL(control_unit_1_p18[3]), .DIV(control_unit_1_p18[2]), .CMP(control_unit_1_p18[1]),
    .LOAD(control_unit_1_p18[0]), .AX_4(alu_1_ax_4), .BX_4(alu_1_bx_4), .CX_4(alu_1_cx_4), .DX_4(alu_1_dx_4),
    .EX_4(alu_1_ex_4), .Zero(alu_1_zero), .Cout(alu_1_cout));
  GENERAL_PURPOSE general_purpose_1 (
    .INPUT(alu_1_ax_4), .INC(undriven_10[8]), .LD(undriven_10[7]), .DEC(undriven_10[6]),
    .SHL(undriven_10[5]), .SHR(undriven_10[4]), .CIL(undriven_10[3]), .CIR(undriven_10[2]),
    .CML(undriven_10[1]), .CLR(undriven_10[0]), .CLK(and_1_out), .OUTPUT(general_purpose_1_output));
  GENERAL_PURPOSE general_purpose_2 (
    .INPUT(alu_1_bx_4), .INC(undriven_11[8]), .LD(undriven_11[7]), .DEC(undriven_11[6]),
    .SHL(undriven_11[5]), .SHR(undriven_11[4]), .CIL(undriven_11[3]), .CIR(undriven_11[2]),
    .CML(undriven_11[1]), .CLR(undriven_11[0]), .CLK(and_1_out), .OUTPUT(general_purpose_2_output));
  GENERAL_PURPOSE general_purpose_3 (
    .INPUT(alu_1_cx_4), .INC(undriven_12[8]), .LD(undriven_12[7]), .DEC(undriven_12[6]),
    .SHL(undriven_12[5]), .SHR(undriven_12[4]), .CIL(undriven_12[3]), .CIR(undriven_12[2]),
    .CML(undriven_12[1]), .CLR(undriven_12[0]), .CLK(and_1_out), .OUTPUT(general_purpose_3_output));
  GENERAL_PURPOSE general_purpose_4 (
    .INPUT(alu_1_dx_4), .INC(undriven_13[8]), .LD(undriven_13[7]), .DEC(undriven_13[6]),
    .SHL(undriven_13[5]), .SHR(undriven_13[4]), .CIL(undriven_13[3]), .CIR(undriven_13[2]),
    .CML(undriven_13[1]), .CLR(undriven_13[0]), .CLK(and_1_out), .OUTPUT(general_purpose_4_output));
  GENERAL_PURPOSE general_purpose_5 (
    .INPUT(alu_1_ex_4), .INC(undriven_14[8]), .LD(undriven_14[7]), .DEC(undriven_14[6]),
    .SHL(undriven_14[5]), .SHR(undriven_14[4]), .CIL(undriven_14[3]), .CIR(undriven_14[2]),
    .CML(undriven_14[1]), .CLR(undriven_14[0]), .CLK(and_1_out), .OUTPUT(general_purpose_5_output));
  Multiplexer #(.select(3), .width(16), .enable("false")) multiplexer_1 (
    .in0(special_purpose_1_output), .in1(general_purpose_1_output), .in2(general_purpose_2_output),
    .in3(general_purpose_3_output), .in4(general_purpose_4_output), .in5(general_purpose_5_output),
    .out(multiplexer_1_out), .sel(control_unit_1_p28));  // open: in6, in7
  assign controlled_buffer_1_out = undriven_18 ? {{8{1'b0}}, general_purpose_1_output} : 24'bz;  // Controlled_Buffer controlled_buffer_1
  assign controlled_buffer_1_out = undriven_19 ? {{8{1'b0}}, general_purpose_2_output} : 24'bz;  // Controlled_Buffer controlled_buffer_2
  assign controlled_buffer_1_out = undriven_20 ? {{8{1'b0}}, general_purpose_3_output} : 24'bz;  // Controlled_Buffer controlled_buffer_3
  assign controlled_buffer_1_out = undriven_21 ? {{8{1'b0}}, general_purpose_4_output} : 24'bz;  // Controlled_Buffer controlled_buffer_4
  assign controlled_buffer_1_out = undriven_2 ? {{8{1'b0}}, general_purpose_5_output} : 24'bz;  // Controlled_Buffer controlled_buffer_5
  SPECIAL_PURPOSE special_purpose_1 (
    .INPUT(controlled_buffer_1_out[15:0]), .INC(1'b0), .LD(undriven_5), .CLK(and_1_out),
    .OUTPUT(special_purpose_1_output));
  SPECIAL_PURPOSE special_purpose_2 (
    .INPUT(controlled_buffer_1_out[15:0]), .INC(undriven_22), .LD(undriven_24), .CLK(and_1_out),
    .OUTPUT(special_purpose_2_output));
  SPECIAL_PURPOSE special_purpose_3 (
    .INPUT(controlled_buffer_1_out[15:0]), .INC(1'b0), .LD(undriven_25), .CLK(and_1_out),
    .OUTPUT(special_purpose_3_output));
  INSTRUCTION_REGISTER instruction_register_1 (
    .INPUT(controlled_buffer_1_out), .LOAD(undriven_23), .CLK(and_1_out),
    .OUTPUT({instruction_register_1_output_2, instruction_register_1_output}));
  RAM #(.addrWidth(16), .dataWidth(24), .bus("separate")) ram_1 (
    .addr(multiplexer_1_out), .din(controlled_buffer_1_out), .data(ram_1_data), .str(control_unit_1_p26),
    .clk(and_1_out));  // open: sel, ld, clr
  assign controlled_buffer_1_out = undriven_6 ? {{8{1'b0}}, special_purpose_1_output} : 24'bz;  // Controlled_Buffer controlled_buffer_6
  assign controlled_buffer_1_out = undriven_3 ? {{8{1'b0}}, special_purpose_2_output} : 24'bz;  // Controlled_Buffer controlled_buffer_7
  assign controlled_buffer_1_out = undriven_4 ? {instruction_register_1_output_2, instruction_register_1_output} : 24'bz;  // Controlled_Buffer controlled_buffer_8
  assign controlled_buffer_1_out = control_unit_1_p27 ? ram_1_data : 24'bz;  // Controlled_Buffer controlled_buffer_9
  // Probe on control_unit_1_p2
  // Probe on control_unit_1_p1
  // Probe on general_purpose_1_output
  // Probe on general_purpose_2_output
  // Probe on general_purpose_3_output
  // Probe on general_purpose_4_output
  // Probe on general_purpose_5_output
  // Probe on controlled_buffer_1_out
  LED CLK (.in(and_1_out));
  // Probe on special_purpose_1_output
  // Probe on special_purpose_2_output
  // Probe on special_purpose_3_output
  // Probe on {instruction_register_1_output_2, instruction_register_1_output}

  // Notes on the sheet:
  //   ZF
  //   CF
  //   ALU
  //   AX
  //   BX
  //   CX
  //   DX
  //   EX
  //   AR
  //   PC
  //   DR
  //   IR
endmodule
